# Fritzing sketch fritz (saved by Fritzing 0.9.4)
breadboards: 1

parts:
  Argon2 = Particle Argon
  Part6 = Adafruit MicroSD card breakout board [part_number="Adafruit #254"]
  OLED_I2C2 = OLED 128x64 I2C Monochrome Display
  Relay1 = Relay - 6 pins [package="DIP (Dual Inline) [THT]"]
  Part7 = Soil Moisture Sensor
  Q1 = PNP-Transistor [package="TO92 [THT]"]
  R1 = Resistor [tolerance=±5% resistance=2.2k package="0603 [SMD]"]
  R2 = Resistor [tolerance=±5% resistance=220 package="0603 [SMD]"]

nets:
  VCC: Argon2.3.3V, Part6.+3V3, OLED_I2C2.VDD, Relay1.VCC, Part7.VCC
  GND: Argon2.GND, Part6.GND, OLED_I2C2.GND, Relay1.GND, Part7.GND, Q1.E, R1.Pin_1
  N1: Argon2.A1, Part7.SIG
  N2: Argon2.A2, Relay1.IN, Q1.C, R2.Pin_1
  N3: Argon2.A4, Part6.CS
  N4: Argon2.SCK, Part6.CLK
  N5: Argon2.MO, Part6.DI
  N6: Argon2.MI, Part6.DO
  N7: Argon2.SDA, OLED_I2C2.SCK
  N8: Argon2.D7, Q1.B, R1.Pin_0
  N9: Argon2.VUSB, Relay1.ON, R2.Pin_0

custom parts:
  Particle Argon: The Argon is a powerful Wi-Fi enabled development board that can act as either a standalone Wi-Fi endpoint or Wi-Fi enabled gateway for Particle Mesh networks. It is based on the Nordic nRF52840 and has built-in battery charging circuitry so it’s easy to connect a Li-Po and deploy your local network in minutes. The Argon is great for connecting existing projects to the Particle Device Cloud or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
  Adafruit MicroSD card breakout board: Not just a simple breakout board, this microSD adapter goes the extra mile - designed for ease of use. Onboard 5v->3v regulator provides 150mA for power-hungry cards 3v level shifting means you can use this with ease on either 3v or 5v systems Uses a proper level shifting chip, not resistors: less problems, and faster read/write access Use 3 or 4 digital pins to read and write 2Gb+ of storage!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
  Relay - 6 pins: A DIP stand-in part for whatever IC you want. With 6 pins on a 900mil dual inline package (DIP) footprint.
